// Logisim project cpu.circ as structural Verilog: 4 circuits, main circuit main
module main (
);

  wire memory_latch_1_oe_latched, memory_latch_1_we_latched;
  wire [15:0] memory_latch_1_address_latched, memory_latch_1_data_in_latched;

  ROM rom_1 ();  // open: addr, data
  memory_latch memory_latch_1 (
    .address_latched(memory_latch_1_address_latched), .WE_latched(memory_latch_1_we_latched),
    .OE_latched(memory_latch_1_oe_latched), .data_in_latched(memory_latch_1_data_in_latched));  // open: address, WE, clk, data_in
  RAM #(.addrWidth(16), .dataWidth(16), .trigger("high"), .databus("bibus")) ram_1 (
    .addr(memory_latch_1_address_latched), .we(memory_latch_1_we_latched), .oe(memory_latch_1_oe_latched),
    .din(memory_latch_1_data_in_latched));  // open: dout
endmodule

module memory_latch (
  input  [15:0] address,
  input  WE,
  input  clk,
  input  [15:0] data_in,
  output [15:0] address_latched,
  output WE_latched,
  output OE_latched,
  output [15:0] data_in_latched
);

  wire DMwe_latch_q;
  wire [15:0] addr_latch_q;

  Register #(.width(16), .trigger("falling")) addr_latch (
    .D(address), .en(WE), .clk(clk), .Q(addr_latch_q));  // open: clr
  D_Flip_Flop #(.trigger("falling")) DMwe_latch (.D(WE), .clk(clk), .Q(DMwe_latch_q));  // open: Qn, preset, reset
  Register #(.width(16), .trigger("falling")) data_to_be_written (
    .D(data_in), .en(WE), .clk(clk), .Q(data_in_latched));  // open: clr
  Multiplexer #(.width(16), .enable("false")) multiplexer_1 (
    .in0(address), .in1(addr_latch_q), .out(address_latched), .sel(DMwe_latch_q));
  and and_1 (WE_latched, clk, DMwe_latch_q);
  not not_1 (OE_latched, WE_latched);
endmodule

module OneReg (
  input  reset,
  input  clk,
  input  WEn,
  input  [15:0] input_16_bit,
  output [15:0] output_16_bit
);

  wire clk_enable;

  D_Flip_Flop d_ff_1 (
    .D(input_16_bit[15]), .clk(clk_enable), .Q(output_16_bit[15]), .reset(reset));  // open: Qn, preset
  D_Flip_Flop d_ff_2 (.D(input_16_bit[7]), .clk(clk_enable), .Q(output_16_bit[7]), .reset(reset));  // open: Qn, preset
  D_Flip_Flop d_ff_3 (
    .D(input_16_bit[14]), .clk(clk_enable), .Q(output_16_bit[14]), .reset(reset));  // open: Qn, preset
  D_Flip_Flop d_ff_4 (.D(input_16_bit[6]), .clk(clk_enable), .Q(output_16_bit[6]), .reset(reset));  // open: Qn, preset
  and and_1 (clk_enable, clk, WEn);
  D_Flip_Flop d_ff_5 (
    .D(input_16_bit[13]), .clk(clk_enable), .Q(output_16_bit[13]), .reset(reset));  // open: Qn, preset
  D_Flip_Flop d_ff_6 (.D(input_16_bit[5]), .clk(clk_enable), .Q(output_16_bit[5]), .reset(reset));  // open: Qn, preset
  D_Flip_Flop d_ff_7 (
    .D(input_16_bit[12]), .clk(clk_enable), .Q(output_16_bit[12]), .reset(reset));  // open: Qn, preset
  D_Flip_Flop d_ff_8 (.D(input_16_bit[4]), .clk(clk_enable), .Q(output_16_bit[4]), .reset(reset));  // open: Qn, preset
  D_Flip_Flop d_ff_9 (
    .D(input_16_bit[11]), .clk(clk_enable), .Q(output_16_bit[11]), .reset(reset));  // open: Qn, preset
  D_Flip_Flop d_ff_10 (.D(input_16_bit[3]), .clk(clk_enable), .Q(output_16_bit[3]), .reset(reset));  // open: Qn, preset
  D_Flip_Flop d_ff_11 (
    .D(input_16_bit[10]), .clk(clk_enable), .Q(output_16_bit[10]), .reset(reset));  // open: Qn, preset
  D_Flip_Flop d_ff_12 (.D(input_16_bit[2]), .clk(clk_enable), .Q(output_16_bit[2]), .reset(reset));  // open: Qn, preset
  D_Flip_Flop d_ff_13 (.D(input_16_bit[9]), .clk(clk_enable), .Q(output_16_bit[9]), .reset(reset));  // open: Qn, preset
  D_Flip_Flop d_ff_14 (.D(input_16_bit[1]), .clk(clk_enable), .Q(output_16_bit[1]), .reset(reset));  // open: Qn, preset
  D_Flip_Flop d_ff_15 (.D(input_16_bit[8]), .clk(clk_enable), .Q(output_16_bit[8]), .reset(reset));  // open: Qn, preset
  D_Flip_Flop d_ff_16 (.D(input_16_bit[0]), .clk(clk_enable), .Q(output_16_bit[0]), .reset(reset));  // open: Qn, preset

  // Other names for the same wires on the sheet: enable = WEn; In0 = input_16_bit[0]; In1 = input_16_bit[1];
  //   In2 = input_16_bit[2]; In3 = input_16_bit[3]; In4 = input_16_bit[4]; In5 = input_16_bit[5];
  //   In6 = input_16_bit[6]; In7 = input_16_bit[7]; In8 = input_16_bit[8]; In9 = input_16_bit[9];
  //   In10 = input_16_bit[10]; In11 = input_16_bit[11]; In12 = input_16_bit[12]; In13 = input_16_bit[13];
  //   In14 = input_16_bit[14]; In15 = input_16_bit[15]; R0 = output_16_bit[0]; R1 = output_16_bit[1];
  //   R2 = output_16_bit[2]; R3 = output_16_bit[3]; R4 = output_16_bit[4]; R5 = output_16_bit[5];
  //   R6 = output_16_bit[6]; R7 = output_16_bit[7]; R8 = output_16_bit[8]; R9 = output_16_bit[9];
  //   R10 = output_16_bit[10]; R11 = output_16_bit[11]; R12 = output_16_bit[12]; R13 = output_16_bit[13];
  //   R14 = output_16_bit[14]; R15 = output_16_bit[15]
endmodule

module RegFile (
  input  in_1
);

  OneReg reg0 ();  // open: reset, clk, WEn, input_16_bit, output_16_bit
endmodule
